# Fritzing sketch Schema (saved by Fritzing 1.0.5)
perfboards: 1

parts:
  Waage = HX711 Weighing Sensor Module
  Q1 = TRANSISTOR_NPN [package=to-92-ammo]
  Q2 = TRANSISTOR_NPN [package=to-92-ammo]
  J1 = Basic Servo
  Buck = RioRand LM2596
  V1 = DC Power [voltage=12V internal_resistance=0.1Ω]
  Oled = Grove OLED 128x96
  Arduino = Arduino Uno (Rev3)
  LED1 = LED - 5mm [color="Red (633nm)" current=0.030A package="5 mm [THT]"]
  R3 = Resistor [tolerance=±5% power=0.25W resistance=220 package=THT]
  R4 = Resistor [tolerance=±5% power=0.25W resistance=220 package=THT]
  Button_Plus = Round Pushbutton
  Button_Minus = Round Pushbutton
  Button_Start = Round Pushbutton
  8V_In = Screw terminal - 2 pins [package=THT]
  Display = screw terminal, 4 pins
  Led_Red = Screw terminal - 2 pins [package=THT]
  Led_Green = Screw terminal - 2 pins [package=THT]
  Scale = screw terminal, 4 pins
  Load_Cell1 = Load Cell - Red/white/black/green
  R5 = Resistor [tolerance=±5% power=0.25W resistance=220 package=THT]
  Button_Plus1 = Round Pushbutton
  Led_Green1 = Screw terminal - 2 pins [package=THT]
  Led_Red1 = Screw terminal - 2 pins [package=THT]
  LED2 = LED - 5mm [color="Green (560nm)" current=0.030A package="5 mm [THT]"]
  Scale1 = screw terminal, 4 pins
  Display1 = screw terminal, 4 pins
  Btn_Start = female pin header, 2 pins [form="♀ (female)"]
  Btn_- = female pin header, 2 pins [form="♀ (female)"]
  Btn_+ = female pin header, 2 pins [form="♀ (female)"]
  Btn_Reserve = female pin header, 2 pins [form="♀ (female)"]
  Btn_Start1 = male pin header, 2 pins [form="♂ (male)"]
  Btn_-1 = male pin header, 2 pins [form="♂ (male)"]
  Btn_+1 = male pin header, 2 pins [form="♂ (male)"]
  Btn_Reserve1 = male pin header, 2 pins [form="♂ (male)"]
  Servo = female pin header, 3 pins [form="♀ (female)"]
  Servo2 = male pin header, 3 pins [form="♂ (male)"]
  R1 = Resistor [tolerance=±5% power=0.25W resistance=220 package=THT]
  R2 = Resistor [tolerance=±5% power=0.25W resistance=220 package=THT]

nets:
  5V: Waage.VCC, Arduino.5V, R1.Pin_1, R2.Pin_1
  GND: Waage.GND, Q1.E, Q2.E, Buck.Pin_4, Arduino.GND, 8V_In.pin1, Display.pin1, Btn_Start.pin1, Btn_-.pin1, Btn_+.pin1, Btn_Reserve.pin1, Servo.pin3
  N1: Waage.DO/RX, Arduino.D2
  N2: Waage.CK/TX, Arduino.D3_PWM
  N3: Waage.E+, Scale.pin4
  N4: Waage.E-, Scale.pin3
  N5: Waage.A+, Scale.pin2
  N6: Waage.A-, Scale.pin1
  N7: Q1.B, R4.Pin_1
  N8: Q1.C, Led_Green.pin1
  N9: Q2.B, R3.Pin_1
  N10: Q2.C, Led_Red.pin1
  N11: J1.gnd, Servo2.pin1
  N12: J1.vcc, Servo2.pin2
  N13: J1.pulse, Servo2.pin3
  N14: Buck.Pin_1, V1.V+
  N15: Buck.Pin_2, V1.V-
  8V: Buck.Pin_3, Arduino.VIN, 8V_In.pin2, Servo.pin2
  N16: Oled.GND, Display1.pin4
  N17: Oled.VCC, Display1.pin3
  N18: Oled.SDA, Display1.pin2
  N19: Oled.SCL, Display1.pin1
  N20: Arduino.A0, Btn_Start.pin2
  N21: Arduino.A1, Btn_-.pin2
  N22: Arduino.A2, Btn_+.pin2
  N23: Arduino.A3, Btn_Reserve.pin2
  N24: Arduino.A4/SDA, Display.pin4
  N25: Arduino.A5/SCL, Display.pin3
  N26: Arduino.D4, R3.Pin_0
  N27: Arduino.D5_PWM, R4.Pin_0
  N28: Arduino.D6_PWM, R5.Pin_0
  N29: Arduino.3V3, Display.pin2
  N30: LED1.cathode, Led_Red1.pin2
  N31: LED1.anode, Led_Red1.pin1
  N32: Button_Plus.leg0, Btn_+1.pin1
  N33: Button_Plus.leg1, Btn_+1.pin2
  N34: Button_Minus.leg0, Btn_-1.pin1
  N35: Button_Minus.leg1, Btn_-1.pin2
  N36: Button_Start.leg0, Btn_Start1.pin1
  N37: Button_Start.leg1, Btn_Start1.pin2
  N38: Led_Red.pin2, R1.Pin_0
  N39: Led_Green.pin2, R2.Pin_0
  N40: Load_Cell1.wire1, Scale1.pin1
  N41: Load_Cell1.wire2, Scale1.pin3
  N42: Load_Cell1.wire3, Scale1.pin2
  N43: Load_Cell1.wire4, Scale1.pin4
  N44: R5.Pin_1, Servo.pin1
  N45: Button_Plus1.leg0, Btn_Reserve1.pin1
  N46: Button_Plus1.leg1, Btn_Reserve1.pin2
  N47: Led_Green1.pin1, LED2.anode
  N48: Led_Green1.pin2, LED2.cathode

custom parts:
  Load Cell - Red/white/black/green: A rectangle load cell/weighting pressure Sensor with four wires - Red, white, black, green. Normally corresponding with E+, E-, A+, A- respectively.
